# Fritzing sketch P10_00_00-Main (saved by Fritzing 0.9.3b)
breadboards: 1

parts:
  U1 = attiny85 [package=dip]
  Q2 = npn-Powertransistor [package="TO220 [THT]"]
  S2 = Pushbutton [package=THT]
  LED1 = LED - 3mm [color="Red (633nm)" package="3 mm [THT]"]
  M1 = DC Motor
  Power_plug1 = Power plug
  R1 = Resistor [tolerance=±5% resistance=12k package=THT]
  D1 = Rectifier Diode [part_number=1N4001 package="300 mil [THT]"]
  R3 = Resistor [tolerance=±5% resistance=330 package=THT]
  R4 = Resistor [tolerance=±5% resistance=220k package=THT]

nets:
  N1: U1.Pin_4, Q2.emitter, S2.leg1, LED1.cathode, Power_plug1.GND
  N2: U1.Pin_5, R1.Pin_0
  N3: U1.Pin_6, S2.leg0, R4.Pin_0
  N4: U1.Pin_7, R3.Pin_1
  N5: U1.Pin_8, M1.pin_1, Power_plug1.VCC, D1.cathode, R4.Pin_1
  N6: Q2.base, R1.Pin_1
  N7: Q2.collector, M1.pin_2, D1.anode
  N8: LED1.anode, R3.Pin_0
